# Fritzing sketch circuit_test (saved by Fritzing 0.9.6b)
breadboards: 1

parts:
  Part5 = I2C level shifter bidirectional
  Mod2 = Raspberry Pi 4B
  Part4 = Arduino Nano (Rev3.0)

nets:
  GND: Part5.GND, Mod2.GND
  N1: Part5.LV, Mod2.3V3
  N2: Part5.LV2, Mod2.GPIO21
  N3: Part5.LV1, Mod2.GPIO20
  N4: Part5.HV1, Part4.D4
  N5: Part5.HV2, Part4.D2
  N6: Part5.HV, Mod2.5V
